# Fritzing sketch Fritzing.coche (saved by Fritzing 0.9.3b)
breadboards: 1

parts:
  Componente1 = Arduino Uno (Rev3)
  Componente2 = Bluetooth HC-05 Macho
  HC-SR04_Sensor_1 = HC-SR04 Ultrasonic Distance Sensor
  IC1 = L293D [package=THT]
  VCC1 = Battery block 9V
  M1 = DC Motor
  M2 = DC Motor
  HC-SR04_Sensor_2 = HC-SR04 Ultrasonic Distance Sensor
  LED2 = smd LED [color="Red (633nm)" package="0805 [SMD]"]
  R2 = Resistor [tolerance=±5% resistance=220 package="0402 [SMD]"]

nets:
  N1: Componente1.D8, IC1.Enable_2
  N2: Componente1.D9_PWM, IC1.In_2
  N3: Componente1.D10_PWM/SS, IC1.In_4
  N4: Componente1.D11_PWM/MOSI, IC1.In_3
  N5: Componente1.D12/MISO, HC-SR04_Sensor_2.GND
  N6: Componente1.D13/SCK, HC-SR04_Sensor_2.TRIG
  GND: Componente1.GND, Componente2.GND, HC-SR04_Sensor_1.ECHO, IC1.0V, VCC1.+, HC-SR04_Sensor_2.ECHO, LED2.anode
  N7: Componente1.D0/RX, Componente2.Key
  N8: Componente1.D1/TX, Componente2.RXD
  N9: Componente1.D2, R2.Pin_0
  N10: Componente1.D3_PWM, HC-SR04_Sensor_1.GND
  N11: Componente1.D4, HC-SR04_Sensor_1.TRIG
  N12: Componente1.D5_PWM, IC1.Enable_1
  N13: Componente1.D6_PWM, IC1.In_1
  VCC: Componente1.5V, Componente2.VCC, HC-SR04_Sensor_1.VCC, IC1.+V, HC-SR04_Sensor_2.VCC
  N14: IC1.Out_1_(_Controlled_by_Enable_1_), M1.pin_1
  N15: IC1.Out_2_(_Controlled_by_Enable_1_), M1.pin_2
  N16: IC1.+Vmotor, VCC1.-
  N17: IC1.Out_3_(_Controlled_by_Enable_2_), M2.pin_2
  N18: IC1.Out_4_(_Controlled_by_Enable_2_), M2.pin_1
  N19: LED2.cathode, R2.Pin_1
